# Fritzing sketch ardor (saved by Fritzing 0.9.3b)
circuit board: 6cm x 4cm
breadboards: 1

parts:
  J3 = Screw terminal - 2 pins [package=THT]
  J1 = female pin header, 3 pins [form="♀ (female)"]
  J4 = Screw terminal - 2 pins [package=THT]
  Part1 = Arduino Nano (Rev3.0)
  R2 = Resistor [tolerance=±5% resistance=10k package=THT]
  R1 = Resistor [tolerance=±5% resistance=10k package=THT]
  R3 = Resistor [tolerance=±1% resistance=220 package=THT]
  J2 = screw terminal, 2 pins

nets:
  N1: J3.pin1, J1.pin2, Part1.5V, J2.pin1
  N2: J3.pin2, Part1.D11/MOSI, R1.Pin_1
  N3: J1.pin1, Part1.D8
  N4: J1.pin3, J4.pin1, Part1.GND, R2.Pin_0, R1.Pin_0
  N5: J4.pin2, R3.Pin_1
  N6: Part1.D9, R3.Pin_0
  N7: Part1.D10, R2.Pin_1, J2.pin2

notes:
  led
  gate
  btn
  / + -
